# Fritzing sketch neildeighan-blog-pronguino-4-circuit-fritzing (saved by Fritzing 0.9.4)
circuit board: 7.61428cm x 7.77728cm
breadboards: 1

parts:
  Part1 = Arduino Uno (Rev3)
  R1 = Trimmer Potentiometer [maximum_resistance=10kΩ package=THT]
  R2 = Trimmer Potentiometer [maximum_resistance=10kΩ package=THT]
  S2 = Pushbutton [package="[THT]"]
  S1 = Pushbutton [package="[THT]"]
  R4 = Resistor [tolerance=±5% resistance=10k package=THT]
  R3 = Resistor [tolerance=±5% resistance=10k package=THT]
  LED1 = LED - 5mm [color="Yellow (592nm)" package="5 mm [THT]"]
  R5 = Resistor [tolerance=±5% resistance=220 package=THT]
  R6 = Resistor [tolerance=±5% resistance=220 package=THT]
  LED2 = LED - 5mm [color="Yellow (592nm)" package="5 mm [THT]"]

nets:
  N1: Part1.A1, R1.wiper
  N2: Part1.A2, R2.wiper
  N3: Part1.GND, R1.leg1, R2.leg1, R4.Pin_1, R3.Pin_0, R5.Pin_1, R6.Pin_1
  N4: Part1.D2, S1.Pin_3, S1.Pin_4, R3.Pin_1
  N5: Part1.D3_PWM, S2.Pin_3, S2.Pin_4, R4.Pin_0
  N6: Part1.D4, LED1.anode
  N7: Part1.D5_PWM, LED2.anode
  N8: Part1.5V, R1.leg2, R2.leg2, S2.Pin_1, S2.Pin_2, S1.Pin_1, S1.Pin_2
  N9: LED1.cathode, R5.Pin_0
  N10: R6.Pin_0, LED2.cathode
